# Fritzing sketch AES_PCB (saved by Fritzing 0.9.4)
breadboards: 1

parts:
  Part1 = Arduino Mega 2560 (Rev3)
  S1 = Pushbutton [package="[THT]"]
  S2 = Pushbutton [package="[THT]"]
  S3 = Pushbutton [package="[THT]"]
  S4 = Pushbutton [package="[THT]"]
  R1 = Resistor [tolerance=±5% resistance=10k package=THT]
  R4 = Resistor [tolerance=±5% resistance=10k package=THT]
  R5 = Resistor [tolerance=±5% resistance=10k package=THT]
  R6 = Resistor [tolerance=±5% resistance=10k package=THT]
  R7 = Trimmer Potentiometer [maximum_resistance=10kΩ package=THT]
  Part2 = Thumb Joystick
  DFRobot_DFPlayer_Mini1 = DFRobot DFPlayer Mini [part_number=DFR0299]
  SP1 = SPEAKER [package=pcb_mount_speaker]
  R8 = Resistor [tolerance=±5% resistance=1k package=THT]
  U2 = M10X2 [package=2x10_lock_special]

nets:
  N1: Part1.A0, Part2.HORZ
  N2: Part1.A1, Part2.VERT
  N3: Part1.A2, R7.wiper
  N4: Part1.D13_PWM, DFRobot_DFPlayer_Mini1.TX
  N5: Part1.D12_PWM, R8.Pin_1
  N6: Part1.D11_PWM, S1.Pin_1, S1.Pin_2, R1.Pin_0
  N7: Part1.D10_PWM, S2.Pin_1, S2.Pin_2, R4.Pin_0
  N8: Part1.D9_PWM, S3.Pin_1, S3.Pin_2, R5.Pin_0
  N9: Part1.D8_PWM, S4.Pin_1, S4.Pin_2, R6.Pin_0
  VCC: Part1.5V, S1.Pin_3, S1.Pin_4, S2.Pin_3, S2.Pin_4, S3.Pin_3, S3.Pin_4, S4.Pin_3, S4.Pin_4, R7.leg2, Part2.VCC, DFRobot_DFPlayer_Mini1.VCC
  GND: Part1.GND, R1.Pin_1, R4.Pin_1, R6.Pin_1, R7.leg1, Part2.GND, DFRobot_DFPlayer_Mini1.GND-1, DFRobot_DFPlayer_Mini1.GND-2, U2.19, U2.20
  N10: Part1.D36, U2.1
  N11: Part1.D37, U2.2
  N12: Part1.D38, U2.3
  N13: Part1.D39, U2.4
  N14: Part1.D40, U2.5
  N15: Part1.D41, U2.6
  N16: Part1.D42, U2.7
  N17: Part1.D43, U2.8
  N18: Part1.D44, U2.9
  N19: Part1.D45, U2.10
  N20: Part1.D46, U2.11
  N21: Part1.D47, U2.12
  N22: Part1.D48, U2.13
  N23: Part1.D49, U2.14
  N24: Part1.D50, U2.15
  N25: Part1.D51, U2.16
  N26: Part1.D52, U2.17
  N27: Part1.D53, U2.18
  N28: DFRobot_DFPlayer_Mini1.RX, R8.Pin_0
  N29: DFRobot_DFPlayer_Mini1.SPK_1, SP1.+
  N30: DFRobot_DFPlayer_Mini1.SPK_2, SP1.-
